// Logisim project EncoderPre .circ as structural Verilog: 1 circuit, main circuit main
module main (
  input  A0,
  input  A_1,
  input  A_2,
  input  A_3,
  output B_0,
  output B_1
);

  wire not_1_out, not_2_out, priority_encoder_1_gs, priority_encoder_2_gs;

  not not_1 (not_1_out, A0);
  not not_2 (not_2_out, A_1);
  Priority_Encoder #(.select(2)) priority_encoder_1 (
    .in0(not_1_out), .in3(A0), .gs(priority_encoder_1_gs));  // open: in1, in2, out, en_out, en_in
  Priority_Encoder #(.select(2)) priority_encoder_2 (
    .in0(not_2_out), .in3(A_1), .gs(priority_encoder_2_gs));  // open: in1, in2, out, en_out, en_in
endmodule
