// Logisim project decoder.circ as structural Verilog: 1 circuit, main circuit main
module main (
  input  B0,
  input  B1,
  output A0,
  output A3,
  output A1,
  output A2
);

  wire and_1_out, and_2_out, and_3_out, and_4_out, not_1_out, not_2_out, or_1_out, or_2_out;

  not not_1 (not_1_out, B0);
  not not_2 (not_2_out, B1);
  and and_1 (and_1_out, not_1_out, not_2_out);
  and and_2 (and_2_out, B0, not_2_out);
  and and_3 (and_3_out, B1, not_1_out);
  and and_4 (and_4_out, B1, B0);
  or or_1 (or_1_out, and_2_out, and_3_out);
  or or_2 (or_2_out, and_1_out, and_4_out);
endmodule
