// Logisim project demux.circ as structural Verilog
module main (
  input  I,
  input  S_1,
  input  S_0,
  output Y0,
  output Y1,
  output Y2,
  output Y3
);

  wire demultiplexer_1_out0, demultiplexer_1_out3, demultiplexer_2_out0, demultiplexer_2_out3, not_1_out;
  wire [1:1] undriven;

  not not_1 (not_1_out, S_1);
  Demultiplexer #(.select(2)) demultiplexer_1 (
    .out0(demultiplexer_1_out0), .out3(demultiplexer_1_out3), .in(I), .sel({undriven[1], S_0}), .en(not_1_out));  // open: out1, out2
  Demultiplexer #(.select(2)) demultiplexer_2 (
    .out0(demultiplexer_2_out0), .out3(demultiplexer_2_out3), .in(I), .sel({undriven[1], S_0}), .en(S_1));  // open: out1, out2
  // Pins of 1 and 2 bits meet at {undriven[1], S_0}
endmodule
