// Logisim project 2.circ as structural Verilog: 1 circuit, main circuit main
module main (
  input  E,
  input  I,
  input  S_0,
  output X0,
  output X1
);

  wire and_1_out, and_2_out, not_1_out;

  not not_1 (not_1_out, S_0);
  and and_1 (and_1_out, E, not_1_out, I);
  and and_2 (and_2_out, E, I, S_0);
endmodule
