// Logisim project encoder.circ as structural Verilog: 1 circuit, main circuit main
module main (
  input  I_3,
  input  I_2,
  input  B,
  input  I_1,
  input  I_0,
  output A
);

  wire or_1_out, or_2_out;

  or or_1 (or_1_out, I_3, I_2);
  or or_2 (or_2_out, I_3, I_1);
endmodule
