// Logisim project 1-bit ALU.circ as structural Verilog: 1 circuit, main circuit main
module main (
  input  Cin,
  input  M,
  input  A,
  input  B,
  input  [1:0] S_0,
  output Output,
  output Cout
);

  wire and_1_out, and_2_out, and_3_out, and_4_out, and_5_out, decoder_1_out0, decoder_1_out2, decoder_1_out3,
       multiplexer_1_out, not_1_out, or_1_out, xnor_1_out, xor_1_out, xor_2_out, xor_3_out, xor_4_out,
       xor_5_out;

  Decoder #(.select(2), .enable("false")) decoder_1 (
    .out0(decoder_1_out0), .out2(decoder_1_out2), .out3(decoder_1_out3), .sel(S_0));  // open: out1
  xor xor_1 (xor_1_out, B, decoder_1_out2);
  and and_1 (and_1_out, xor_1_out, not_1_out);
  not not_1 (not_1_out, decoder_1_out0);
  and and_2 (and_2_out, A, B);
  or or_1 (or_1_out, A, B);
  xor xor_2 (xor_2_out, A, B);
  xnor xnor_1 (xnor_1_out, B, A);
  xor xor_3 (xor_3_out, decoder_1_out3, A);
  xor xor_4 (xor_4_out, and_1_out, xor_3_out);
  and and_3 (and_3_out, M, xor_3_out, and_1_out);
  or or_2 (Cout, and_3_out, and_4_out);
  Multiplexer #(.select(2), .enable("false")) multiplexer_1 (
    .in0(and_2_out), .in1(or_1_out), .in2(xor_2_out), .in3(xnor_1_out), .out(multiplexer_1_out), .sel(S_0));
  xor xor_5 (xor_5_out, Cin, xor_4_out);
  and and_4 (and_4_out, M, Cin, xor_4_out);
  and and_5 (and_5_out, xor_5_out, M);
  Multiplexer #(.enable("false")) multiplexer_2 (.in0(multiplexer_1_out), .in1(and_5_out), .out(Output), .sel(M));
endmodule
