// Logisim project 4-bit ALU.circ as structural Verilog: 1 circuit, main circuit main
module main (
  input  Cin,
  input  M,
  input  [1:0] S_0_1,
  input  [3:0] A,
  input  [3:0] B,
  output [3:0] out_6,
  output Cout
);

  wire adder_1_cout, subtractor_1_bout, subtractor_2_bout;
  wire [3:0] adder_1_out, and_1_out, multiplexer_1_out, multiplexer_2_out, or_1_out, subtractor_1_out,
       subtractor_2_out, xnor_1_out, xor_1_out;

  assign and_1_out = A & B;  // AND_Gate and_1, 4 bits wide
  assign or_1_out = A | B;  // OR_Gate or_1, 4 bits wide
  assign xor_1_out = A ^ B;  // XOR_Gate xor_1, 4 bits wide
  assign xnor_1_out = ~(A ^ B);  // XNOR_Gate xnor_1, 4 bits wide
  Adder #(.width(4)) adder_1 (.a(A), .b(B), .out(adder_1_out), .cin(Cin), .cout(adder_1_cout));
  Subtractor #(.width(4)) subtractor_1 (.a(A), .b(B), .out(subtractor_1_out), .bin(Cin), .bout(subtractor_1_bout));
  Subtractor #(.width(4)) subtractor_2 (.a(B), .b(A), .out(subtractor_2_out), .bin(Cin), .bout(subtractor_2_bout));
  Multiplexer #(.select(2), .width(4), .enable("false")) multiplexer_1 (
    .in0(and_1_out), .in1(or_1_out), .in2(xor_1_out), .in3(xnor_1_out), .out(multiplexer_1_out), .sel(S_0_1));
  Multiplexer #(.select(2), .width(4), .enable("false")) multiplexer_2 (
    .in0(A), .in1(adder_1_out), .in2(subtractor_1_out), .in3(subtractor_2_out), .out(multiplexer_2_out),
    .sel(S_0_1));
  Multiplexer #(.select(2), .enable("false")) multiplexer_3 (
    .in0(Cin), .in1(adder_1_cout), .in2(subtractor_1_bout), .in3(subtractor_2_bout), .out(Cout), .sel(S_0_1));
  Multiplexer #(.width(4), .enable("false")) multiplexer_4 (
    .in0(multiplexer_1_out), .in1(multiplexer_2_out), .out(out_6), .sel(M));
endmodule
