// Logisim project ArithmeticUnit.circ as structural Verilog: 1 circuit, main circuit main
module main (
  input  [1:0] S_0,
  input  A,
  input  Cin,
  input  B,
  output Output,
  output Cout
);

  wire and_1_out, and_2_out, and_3_out, decoder_1_out0, decoder_1_out1, decoder_1_out2, decoder_1_out3,
       not_1_out, xor_1_out, xor_2_out, xor_3_out;

  Decoder #(.select(2), .enable("false")) decoder_1 (
    .out0(decoder_1_out0), .out1(decoder_1_out1), .out2(decoder_1_out2), .out3(decoder_1_out3), .sel(S_0));
  not not_1 (not_1_out, decoder_1_out0);
  and and_1 (and_1_out, B, not_1_out);
  xor xor_1 (xor_1_out, and_1_out, decoder_1_out2);
  xor xor_2 (xor_2_out, A, decoder_1_out3);
  xor xor_3 (xor_3_out, xor_2_out, xor_1_out);
  and and_2 (and_2_out, xor_1_out, xor_2_out);
  or or_1 (Cout, and_2_out, and_3_out);
  xor xor_4 (Output, Cin, xor_3_out);
  and and_3 (and_3_out, Cin, xor_3_out);
  // also tied to GND on the sheet: decoder_1_out1
endmodule
