// Logisim project Logic unit.circ as structural Verilog: 1 circuit, main circuit main
module main (
  input  A,
  input  B,
  input  [1:0] S_0,
  output out_4
);

  wire and_1_out, or_1_out, xnor_1_out, xor_1_out;

  and and_1 (and_1_out, A, B);
  or or_1 (or_1_out, A, B);
  xor xor_1 (xor_1_out, A, B);
  xnor xnor_1 (xnor_1_out, B, A);
  Multiplexer #(.select(2), .enable("false")) multiplexer_1 (
    .in0(and_1_out), .in1(or_1_out), .in2(xor_1_out), .in3(xnor_1_out), .out(out_4), .sel(S_0));
endmodule
